# Fritzing sketch led_bridge_lamp_fritzing_schematics (saved by Fritzing 0.9.3b)
breadboards: 1

parts:
  Part1 = Arduino Uno (Rev3)
  NEOPIXEL1 = Neopixel Strip -- Black (60/m)
  ENCODER2 = Rotary Encoder with Knob bth

nets:
  GND: Part1.GND, NEOPIXEL1.GND
  N1: Part1.D2, NEOPIXEL1.+5V
  N2: Part1.D4, ENCODER2.S
  N3: Part1.D5_PWM, ENCODER2.A
  N4: Part1.D6_PWM, ENCODER2.B
  5V: Part1.5V, NEOPIXEL1.DI, ENCODER2.VIN

custom parts:
  Neopixel Strip -- Black (60/m): Neopixel Strip, Black, 60 pixels per meter.
  Rotary Encoder with Knob bth: Rotary Encoder with 1/4" Shaft and Knob
